# Fritzing sketch AltiTiny (saved by Fritzing 0.9.4)

parts:
  M1 = BMP280
  Digispark1 = Digispark
  J2 = Dagu DGServo 9g header connector (female) [package=THT]

nets:
  VIN: M1.VIN, Digispark1.VCC
  GND: M1.GND, J2.gnd
  N1: M1.SCL, Digispark1.P2
  N2: M1.SDA, Digispark1.P0
  N3: Digispark1.P3, J2.pulse

notes:
  Frsky Hub port
  Altimetre AtTiny45 et BMP280

custom parts:
  BMP280: Temperature Humidity Barometric presure Sensor, I2C
  Digispark: The Digispark is an Attiny85 based microcontroller development board similar to the Arduino line, only cheaper, smaller, and a bit less powerful. With a whole host of shields to extend its functionality and the ability to use the familiar Arduino IDE the Digispark is a great way to jump into electronics, or perfect for when an Arduino is too big or too much.
